# Fritzing sketch sender (saved by Fritzing 0.8.5b)
breadboards: 1

parts:
  U1 = attiny85 [package=dip]
  U2 = RF-LINK_TX [package=rf-link_tx]
  R1 = Resistor [tolerance=±5% resistance=10k package=THT]
  S1 = Pushbutton [package="[THT]"]
  S2 = Pushbutton [package="[THT]"]
  R2 = Resistor [tolerance=±5% resistance=10k package=THT]
  LED1 = LED - 5mm [color="Red (633nm)" package="5 mm [THT]"]
  VCC1 = 4 x AAA Battery Mount
  R3 = Resistor [tolerance=±5% resistance=10k package=THT]
  R4 = Resistor [tolerance=±5% resistance=220 package=THT]

nets:
  N1: U1.Pin_1, R3.Pin_0
  N2: U1.Pin_4, U2.GND, R1.Pin_0, R2.Pin_0, VCC1.-, R3.Pin_1, R4.Pin_0
  N3: U1.Pin_5, S2.Pin_1, S2.Pin_2, R2.Pin_1
  N4: U1.Pin_6, R1.Pin_1, S1.Pin_1, S1.Pin_2
  N5: U1.Pin_7, U2.DATA, LED1.anode
  N6: U1.Pin_8, U2.+5V, S1.Pin_3, S1.Pin_4, S2.Pin_3, S2.Pin_4, VCC1.+
  N7: LED1.cathode, R4.Pin_1
